// Logisim project Processador_Arquitetura.circ as structural Verilog: 8 circuits, main circuit main
module main (
);

  Banco_de_Registradores banco_de_registradores_1 ();  // open: D, Clk, A, W, C, B, SA, SB
endmodule

module Banco_de_Registradores (
  input  [31:0] D,
  input  Clk,
  input  [3:0] A,
  input  W,
  input  [3:0] C,
  input  [3:0] B,
  output [31:0] SA,
  output [31:0] SB
);

  wire demultiplexer_1_out1, demultiplexer_1_out2, demultiplexer_1_out3, demultiplexer_1_out4,
       demultiplexer_1_out5, demultiplexer_1_out6, demultiplexer_1_out7, demultiplexer_1_out8,
       demultiplexer_1_out9, demultiplexer_1_out10, demultiplexer_1_out11, demultiplexer_1_out12,
       demultiplexer_1_out13, demultiplexer_1_out14, demultiplexer_1_out15;
  wire [31:0] registrador_32bits_1_s, registrador_32bits_2_s, registrador_32bits_3_s, registrador_32bits_4_s,
       registrador_32bits_5_s, registrador_32bits_6_s, registrador_32bits_7_s, registrador_32bits_8_s,
       registrador_32bits_9_s, registrador_32bits_10_s, registrador_32bits_11_s, registrador_32bits_12_s,
       registrador_32bits_13_s, registrador_32bits_14_s, registrador_32bits_15_s, registrador_32bits_16_s;

  Demultiplexer #(.select(4)) demultiplexer_1 (
    .out1(demultiplexer_1_out1), .out2(demultiplexer_1_out2), .out3(demultiplexer_1_out3),
    .out4(demultiplexer_1_out4), .out5(demultiplexer_1_out5), .out6(demultiplexer_1_out6),
    .out7(demultiplexer_1_out7), .out8(demultiplexer_1_out8), .out9(demultiplexer_1_out9),
    .out10(demultiplexer_1_out10), .out11(demultiplexer_1_out11), .out12(demultiplexer_1_out12),
    .out13(demultiplexer_1_out13), .out14(demultiplexer_1_out14), .out15(demultiplexer_1_out15), .in(W),
    .sel(C));  // open: out0
  Registrador_32bits registrador_32bits_1 (.W0(1'b1), .D({32{1'b0}}), .S(registrador_32bits_1_s));  // open: CLK
  Registrador_32bits registrador_32bits_2 (.W0(demultiplexer_1_out1), .CLK(Clk), .D(D), .S(registrador_32bits_2_s));
  Registrador_32bits registrador_32bits_3 (.W0(demultiplexer_1_out2), .CLK(Clk), .D(D), .S(registrador_32bits_3_s));
  Registrador_32bits registrador_32bits_4 (.W0(demultiplexer_1_out3), .CLK(Clk), .D(D), .S(registrador_32bits_4_s));
  Registrador_32bits registrador_32bits_5 (.W0(demultiplexer_1_out4), .CLK(Clk), .D(D), .S(registrador_32bits_5_s));
  Registrador_32bits registrador_32bits_6 (.W0(demultiplexer_1_out5), .CLK(Clk), .D(D), .S(registrador_32bits_6_s));
  Registrador_32bits registrador_32bits_7 (.W0(demultiplexer_1_out7), .CLK(Clk), .D(D), .S(registrador_32bits_7_s));
  Registrador_32bits registrador_32bits_8 (.W0(demultiplexer_1_out8), .CLK(Clk), .D(D), .S(registrador_32bits_8_s));
  Registrador_32bits registrador_32bits_9 (.W0(demultiplexer_1_out9), .CLK(Clk), .D(D), .S(registrador_32bits_9_s));
  Registrador_32bits registrador_32bits_10 (.W0(demultiplexer_1_out10), .CLK(Clk), .D(D), .S(registrador_32bits_10_s));
  Registrador_32bits registrador_32bits_11 (.W0(demultiplexer_1_out11), .CLK(Clk), .D(D), .S(registrador_32bits_11_s));
  Registrador_32bits registrador_32bits_12 (.W0(demultiplexer_1_out12), .CLK(Clk), .D(D), .S(registrador_32bits_12_s));
  Registrador_32bits registrador_32bits_13 (.W0(demultiplexer_1_out13), .CLK(Clk), .D(D), .S(registrador_32bits_13_s));
  Registrador_32bits registrador_32bits_14 (.W0(demultiplexer_1_out14), .CLK(Clk), .D(D), .S(registrador_32bits_14_s));
  Registrador_32bits registrador_32bits_15 (.W0(demultiplexer_1_out15), .CLK(Clk), .D(D), .S(registrador_32bits_15_s));
  Registrador_32bits registrador_32bits_16 (.W0(demultiplexer_1_out6), .CLK(Clk), .D(D), .S(registrador_32bits_16_s));
  Multiplexer #(.select(4), .width(32)) multiplexer_1 (
    .in0(registrador_32bits_1_s), .in1(registrador_32bits_2_s), .in2(registrador_32bits_3_s),
    .in3(registrador_32bits_4_s), .in4(registrador_32bits_5_s), .in5(registrador_32bits_6_s),
    .in6(registrador_32bits_16_s), .in7(registrador_32bits_7_s), .in8(registrador_32bits_8_s),
    .in9(registrador_32bits_9_s), .in10(registrador_32bits_10_s), .in11(registrador_32bits_11_s),
    .in12(registrador_32bits_12_s), .in13(registrador_32bits_13_s), .in14(registrador_32bits_14_s),
    .in15(registrador_32bits_15_s), .out(SA), .sel(A));
  Multiplexer #(.select(4), .width(32)) multiplexer_2 (
    .in0(registrador_32bits_1_s), .in1(registrador_32bits_2_s), .in2(registrador_32bits_3_s),
    .in3(registrador_32bits_4_s), .in4(registrador_32bits_5_s), .in5(registrador_32bits_6_s),
    .in6(registrador_32bits_16_s), .in7(registrador_32bits_7_s), .in8(registrador_32bits_8_s),
    .in9(registrador_32bits_9_s), .in10(registrador_32bits_10_s), .in11(registrador_32bits_11_s),
    .in12(registrador_32bits_12_s), .in13(registrador_32bits_13_s), .in14(registrador_32bits_14_s),
    .in15(registrador_32bits_15_s), .out(SB), .sel(B));
endmodule

module Registrador_32bits (
  input  W0,
  input  CLK,
  input  [31:0] D,
  output [31:0] S
);

  Registrador_4bits registrador_4bits_1 (.CLK(CLK), .W0(W0), .D0(D[3:0]), .S(S[3:0]));
  Registrador_4bits registrador_4bits_2 (.CLK(CLK), .W0(W0), .D0(D[7:4]), .S(S[7:4]));
  Registrador_4bits registrador_4bits_3 (.CLK(CLK), .W0(W0), .D0(D[11:8]), .S(S[11:8]));
  Registrador_4bits registrador_4bits_4 (.CLK(CLK), .W0(W0), .D0(D[15:12]), .S(S[15:12]));
  Registrador_4bits registrador_4bits_5 (.CLK(CLK), .W0(W0), .D0(D[19:16]), .S(S[19:16]));
  Registrador_4bits registrador_4bits_6 (.CLK(CLK), .W0(W0), .D0(D[23:20]), .S(S[23:20]));
  Registrador_4bits registrador_4bits_7 (.CLK(CLK), .W0(W0), .D0(D[27:24]), .S(S[27:24]));
  Registrador_4bits registrador_4bits_8 (.CLK(CLK), .W0(W0), .D0(D[31:28]), .S(S[31:28]));
endmodule

module Registrador_4bits (
  input  CLK,
  input  W0,
  input  [3:0] D0,
  output [3:0] S
);

  wire multiplexer_1_out, multiplexer_2_out, multiplexer_3_out, multiplexer_4_out;

  Multiplexer multiplexer_1 (.in0(S[0]), .in1(D0[0]), .out(multiplexer_1_out), .sel(W0));
  Multiplexer multiplexer_2 (.in0(S[1]), .in1(D0[1]), .out(multiplexer_2_out), .sel(W0));
  Multiplexer multiplexer_3 (.in0(S[2]), .in1(D0[2]), .out(multiplexer_3_out), .sel(W0));
  Multiplexer multiplexer_4 (.in0(S[3]), .in1(D0[3]), .out(multiplexer_4_out), .sel(W0));
  D_Flip_Flop d_ff_1 (.D(multiplexer_1_out), .clk(CLK), .Q(S[0]));  // open: Qn, preset, reset
  D_Flip_Flop d_ff_2 (.D(multiplexer_2_out), .clk(CLK), .Q(S[1]));  // open: Qn, preset, reset
  D_Flip_Flop d_ff_3 (.D(multiplexer_3_out), .clk(CLK), .Q(S[2]));  // open: Qn, preset, reset
  D_Flip_Flop d_ff_4 (.D(multiplexer_4_out), .clk(CLK), .Q(S[3]));  // open: Qn, preset, reset
endmodule

module full_adder (
  input  A,
  input  B,
  input  Cin,
  output S,
  output Cout
);

  wire and_1_out, and_2_out, and_3_out, xor_1_out;

  xor xor_1 (xor_1_out, B, Cin);
  and and_1 (and_1_out, Cin, B);
  and and_2 (and_2_out, Cin, A);
  and and_3 (and_3_out, B, A);
  xor xor_2 (S, A, xor_1_out);
  or or_1 (Cout, and_1_out, and_2_out, and_3_out);
endmodule

module half_adder (
  input  A,
  input  B,
  output S,
  output Cout
);

  xor xor_1 (S, A, B);
  and and_1 (Cout, A, B);
endmodule

module Somador (
  input  [31:0] A,
  input  [31:0] in_2,
  output [31:0] out_3
);

  wire full_adder_1_cout, full_adder_2_cout, full_adder_3_cout, full_adder_4_cout, full_adder_5_cout,
       full_adder_6_cout, full_adder_7_cout, full_adder_8_cout, full_adder_9_cout, full_adder_10_cout,
       full_adder_11_cout, full_adder_12_cout, full_adder_13_cout, full_adder_14_cout, full_adder_15_cout,
       full_adder_16_cout, full_adder_17_cout, full_adder_18_cout, full_adder_19_cout, full_adder_20_cout,
       full_adder_21_cout, full_adder_22_cout, full_adder_23_cout, full_adder_24_cout, full_adder_25_cout,
       full_adder_26_cout, full_adder_27_cout, full_adder_28_cout, full_adder_29_cout, full_adder_30_cout,
       half_adder_1_cout;

  half_adder half_adder_1 (.A(A[0]), .B(in_2[0]), .S(out_3[0]), .Cout(half_adder_1_cout));
  full_adder full_adder_1 (.A(A[1]), .B(in_2[1]), .Cin(half_adder_1_cout), .S(out_3[1]), .Cout(full_adder_1_cout));
  full_adder full_adder_2 (.A(A[2]), .B(in_2[2]), .Cin(full_adder_1_cout), .S(out_3[2]), .Cout(full_adder_2_cout));
  full_adder full_adder_3 (.A(A[3]), .B(in_2[3]), .Cin(full_adder_2_cout), .S(out_3[3]), .Cout(full_adder_3_cout));
  full_adder full_adder_4 (.A(A[4]), .B(in_2[4]), .Cin(full_adder_3_cout), .S(out_3[4]), .Cout(full_adder_4_cout));
  full_adder full_adder_5 (.A(A[5]), .B(in_2[5]), .Cin(full_adder_4_cout), .S(out_3[5]), .Cout(full_adder_5_cout));
  full_adder full_adder_6 (.A(A[6]), .B(in_2[6]), .Cin(full_adder_5_cout), .S(out_3[6]), .Cout(full_adder_6_cout));
  full_adder full_adder_7 (.A(A[7]), .B(in_2[7]), .Cin(full_adder_6_cout), .S(out_3[7]), .Cout(full_adder_7_cout));
  full_adder full_adder_8 (.A(A[8]), .B(in_2[8]), .Cin(full_adder_7_cout), .S(out_3[8]), .Cout(full_adder_8_cout));
  full_adder full_adder_9 (.A(A[9]), .B(in_2[9]), .Cin(full_adder_8_cout), .S(out_3[9]), .Cout(full_adder_9_cout));
  full_adder full_adder_10 (.A(A[10]), .B(in_2[10]), .Cin(full_adder_9_cout), .S(out_3[10]), .Cout(full_adder_10_cout));
  full_adder full_adder_11 (
    .A(A[11]), .B(in_2[11]), .Cin(full_adder_10_cout), .S(out_3[11]), .Cout(full_adder_11_cout));
  full_adder full_adder_12 (
    .A(A[12]), .B(in_2[12]), .Cin(full_adder_11_cout), .S(out_3[12]), .Cout(full_adder_12_cout));
  full_adder full_adder_13 (
    .A(A[13]), .B(in_2[13]), .Cin(full_adder_12_cout), .S(out_3[13]), .Cout(full_adder_13_cout));
  full_adder full_adder_14 (
    .A(A[14]), .B(in_2[14]), .Cin(full_adder_13_cout), .S(out_3[14]), .Cout(full_adder_14_cout));
  full_adder full_adder_15 (
    .A(A[15]), .B(in_2[15]), .Cin(full_adder_14_cout), .S(out_3[15]), .Cout(full_adder_15_cout));
  full_adder full_adder_16 (
    .A(A[16]), .B(in_2[16]), .Cin(full_adder_15_cout), .S(out_3[16]), .Cout(full_adder_16_cout));
  full_adder full_adder_17 (
    .A(A[17]), .B(in_2[17]), .Cin(full_adder_16_cout), .S(out_3[17]), .Cout(full_adder_17_cout));
  full_adder full_adder_18 (
    .A(A[18]), .B(in_2[18]), .Cin(full_adder_17_cout), .S(out_3[18]), .Cout(full_adder_18_cout));
  full_adder full_adder_19 (
    .A(A[19]), .B(in_2[19]), .Cin(full_adder_18_cout), .S(out_3[19]), .Cout(full_adder_19_cout));
  full_adder full_adder_20 (
    .A(A[20]), .B(in_2[20]), .Cin(full_adder_19_cout), .S(out_3[20]), .Cout(full_adder_20_cout));
  full_adder full_adder_21 (
    .A(A[21]), .B(in_2[21]), .Cin(full_adder_20_cout), .S(out_3[21]), .Cout(full_adder_21_cout));
  full_adder full_adder_22 (
    .A(A[22]), .B(in_2[22]), .Cin(full_adder_21_cout), .S(out_3[22]), .Cout(full_adder_22_cout));
  full_adder full_adder_23 (
    .A(A[23]), .B(in_2[23]), .Cin(full_adder_22_cout), .S(out_3[23]), .Cout(full_adder_23_cout));
  full_adder full_adder_24 (
    .A(A[24]), .B(in_2[24]), .Cin(full_adder_23_cout), .S(out_3[24]), .Cout(full_adder_24_cout));
  full_adder full_adder_25 (
    .A(A[25]), .B(in_2[25]), .Cin(full_adder_24_cout), .S(out_3[25]), .Cout(full_adder_25_cout));
  full_adder full_adder_26 (
    .A(A[26]), .B(in_2[26]), .Cin(full_adder_25_cout), .S(out_3[26]), .Cout(full_adder_26_cout));
  full_adder full_adder_27 (
    .A(A[27]), .B(in_2[27]), .Cin(full_adder_26_cout), .S(out_3[27]), .Cout(full_adder_27_cout));
  full_adder full_adder_28 (
    .A(A[28]), .B(in_2[28]), .Cin(full_adder_27_cout), .S(out_3[28]), .Cout(full_adder_28_cout));
  full_adder full_adder_29 (
    .A(A[29]), .B(in_2[29]), .Cin(full_adder_28_cout), .S(out_3[29]), .Cout(full_adder_29_cout));
  full_adder full_adder_30 (
    .A(A[30]), .B(in_2[30]), .Cin(full_adder_29_cout), .S(out_3[30]), .Cout(full_adder_30_cout));
  full_adder full_adder_31 (.A(A[31]), .B(in_2[31]), .Cin(full_adder_30_cout), .S(out_3[31]));  // open: Cout

  // Other names for the same wires on the sheet: B0 = in_2[0]; B1 = in_2[1]; B2 = in_2[2]; B3 = in_2[3]; B4 = in_2[4];
  //   B5 = in_2[5]; B6 = in_2[6]; B7 = in_2[7]; B8 = in_2[8]; B9 = in_2[9]; B10 = in_2[10]; B11 = in_2[11];
  //   B12 = in_2[12]; B13 = in_2[13]; B14 = in_2[14]; B15 = in_2[15]; B16 = in_2[16]; B17 = in_2[17]; B18 = in_2[18];
  //   B19 = in_2[19]; B20 = in_2[20]; B21 = in_2[21]; B22 = in_2[22]; B23 = in_2[23]; B24 = in_2[24]; B25 = in_2[25];
  //   B26 = in_2[26]; B27 = in_2[27]; B28 = in_2[28]; B29 = in_2[29]; B30 = in_2[30]; B31 = in_2[31]; S0 = out_3[0];
  //   S1 = out_3[1]; S2 = out_3[2]; S3 = out_3[3]; S4 = out_3[4]; S5 = out_3[5]; S6 = out_3[6]; S7 = out_3[7];
  //   S8 = out_3[8]; S9 = out_3[9]; S10 = out_3[10]; S11 = out_3[11]; S12 = out_3[12]; S13 = out_3[13];
  //   S14 = out_3[14]; S15 = out_3[15]; S16 = out_3[16]; S17 = out_3[17]; S18 = out_3[18]; S19 = out_3[19];
  //   S20 = out_3[20]; S21 = out_3[21]; S22 = out_3[22]; S23 = out_3[23]; S24 = out_3[24]; S25 = out_3[25];
  //   S26 = out_3[26]; S27 = out_3[27]; S28 = out_3[28]; S29 = out_3[29]; S30 = out_3[30]; S31 = out_3[31]
endmodule

module somador_cmpl2 (
  input  [31:0] in_1,
  output [31:0] out_2
);

  wire half_adder_1_cout, half_adder_2_cout, half_adder_3_cout, half_adder_4_cout, half_adder_5_cout,
       half_adder_6_cout, half_adder_7_cout, half_adder_8_cout, half_adder_9_cout, half_adder_10_cout,
       half_adder_11_cout, half_adder_12_cout, half_adder_13_cout, half_adder_14_cout, half_adder_15_cout,
       half_adder_16_cout, half_adder_17_cout, half_adder_18_cout, half_adder_19_cout, half_adder_20_cout,
       half_adder_21_cout, half_adder_22_cout, half_adder_23_cout, half_adder_24_cout, half_adder_25_cout,
       half_adder_26_cout, half_adder_27_cout, half_adder_28_cout, half_adder_29_cout, half_adder_30_cout,
       half_adder_31_cout;

  half_adder half_adder_1 (.A(1'b1), .B(in_1[0]), .S(out_2[0]), .Cout(half_adder_1_cout));
  half_adder half_adder_2 (.A(in_1[1]), .B(half_adder_1_cout), .S(out_2[1]), .Cout(half_adder_2_cout));
  half_adder half_adder_3 (.A(in_1[2]), .B(half_adder_2_cout), .S(out_2[2]), .Cout(half_adder_3_cout));
  half_adder half_adder_4 (.A(in_1[3]), .B(half_adder_3_cout), .S(out_2[3]), .Cout(half_adder_4_cout));
  half_adder half_adder_5 (.A(in_1[4]), .B(half_adder_4_cout), .S(out_2[4]), .Cout(half_adder_5_cout));
  half_adder half_adder_6 (.A(in_1[5]), .B(half_adder_5_cout), .S(out_2[5]), .Cout(half_adder_6_cout));
  half_adder half_adder_7 (.A(in_1[6]), .B(half_adder_6_cout), .S(out_2[6]), .Cout(half_adder_7_cout));
  half_adder half_adder_8 (.A(in_1[7]), .B(half_adder_7_cout), .S(out_2[7]), .Cout(half_adder_8_cout));
  half_adder half_adder_9 (.A(in_1[8]), .B(half_adder_8_cout), .S(out_2[8]), .Cout(half_adder_9_cout));
  half_adder half_adder_10 (.A(in_1[9]), .B(half_adder_9_cout), .S(out_2[9]), .Cout(half_adder_10_cout));
  half_adder half_adder_11 (.A(in_1[10]), .B(half_adder_10_cout), .S(out_2[10]), .Cout(half_adder_11_cout));
  half_adder half_adder_12 (.A(in_1[11]), .B(half_adder_11_cout), .S(out_2[11]), .Cout(half_adder_12_cout));
  half_adder half_adder_13 (.A(in_1[12]), .B(half_adder_12_cout), .S(out_2[12]), .Cout(half_adder_13_cout));
  half_adder half_adder_14 (.A(in_1[13]), .B(half_adder_13_cout), .S(out_2[13]), .Cout(half_adder_14_cout));
  half_adder half_adder_15 (.A(in_1[14]), .B(half_adder_14_cout), .S(out_2[14]), .Cout(half_adder_15_cout));
  half_adder half_adder_16 (.A(in_1[15]), .B(half_adder_15_cout), .S(out_2[15]), .Cout(half_adder_16_cout));
  half_adder half_adder_17 (.A(in_1[16]), .B(half_adder_16_cout), .S(out_2[16]), .Cout(half_adder_17_cout));
  half_adder half_adder_18 (.A(in_1[17]), .B(half_adder_17_cout), .S(out_2[17]), .Cout(half_adder_18_cout));
  half_adder half_adder_19 (.A(in_1[18]), .B(half_adder_18_cout), .S(out_2[18]), .Cout(half_adder_19_cout));
  half_adder half_adder_20 (.A(in_1[19]), .B(half_adder_19_cout), .S(out_2[19]), .Cout(half_adder_20_cout));
  half_adder half_adder_21 (.A(in_1[20]), .B(half_adder_20_cout), .S(out_2[20]), .Cout(half_adder_21_cout));
  half_adder half_adder_22 (.A(in_1[21]), .B(half_adder_21_cout), .S(out_2[21]), .Cout(half_adder_22_cout));
  half_adder half_adder_23 (.A(in_1[22]), .B(half_adder_22_cout), .S(out_2[22]), .Cout(half_adder_23_cout));
  half_adder half_adder_24 (.A(in_1[23]), .B(half_adder_23_cout), .S(out_2[23]), .Cout(half_adder_24_cout));
  half_adder half_adder_25 (.A(in_1[24]), .B(half_adder_24_cout), .S(out_2[24]), .Cout(half_adder_25_cout));
  half_adder half_adder_26 (.A(in_1[25]), .B(half_adder_25_cout), .S(out_2[25]), .Cout(half_adder_26_cout));
  half_adder half_adder_27 (.A(in_1[26]), .B(half_adder_26_cout), .S(out_2[26]), .Cout(half_adder_27_cout));
  half_adder half_adder_28 (.A(in_1[27]), .B(half_adder_27_cout), .S(out_2[27]), .Cout(half_adder_28_cout));
  half_adder half_adder_29 (.A(in_1[28]), .B(half_adder_28_cout), .S(out_2[28]), .Cout(half_adder_29_cout));
  half_adder half_adder_30 (.A(in_1[29]), .B(half_adder_29_cout), .S(out_2[29]), .Cout(half_adder_30_cout));
  half_adder half_adder_31 (.A(in_1[30]), .B(half_adder_30_cout), .S(out_2[30]), .Cout(half_adder_31_cout));
  half_adder half_adder_32 (.A(in_1[31]), .B(half_adder_31_cout), .S(out_2[31]));  // open: Cout

  // Other names for the same wires on the sheet: B0 = in_1[0]; B1 = in_1[1]; B2 = in_1[2]; B3 = in_1[3]; B4 = in_1[4];
  //   B5 = in_1[5]; B6 = in_1[6]; B7 = in_1[7]; B8 = in_1[8]; B9 = in_1[9]; B10 = in_1[10]; B11 = in_1[11];
  //   B12 = in_1[12]; B13 = in_1[13]; B14 = in_1[14]; B15 = in_1[15]; B16 = in_1[16]; B17 = in_1[17]; B18 = in_1[18];
  //   B19 = in_1[19]; B20 = in_1[20]; B21 = in_1[21]; B22 = in_1[22]; B23 = in_1[23]; B24 = in_1[24]; B25 = in_1[25];
  //   B26 = in_1[26]; B27 = in_1[27]; B28 = in_1[28]; B29 = in_1[29]; B30 = in_1[30]; B31 = in_1[31]; S0 = out_2[0];
  //   S1 = out_2[1]; S2 = out_2[2]; S3 = out_2[3]; S4 = out_2[4]; S5 = out_2[5]; S6 = out_2[6]; S7 = out_2[7];
  //   S8 = out_2[8]; S9 = out_2[9]; S10 = out_2[10]; S11 = out_2[11]; S12 = out_2[12]; S13 = out_2[13];
  //   S14 = out_2[14]; S15 = out_2[15]; S16 = out_2[16]; S17 = out_2[17]; S18 = out_2[18]; S19 = out_2[19];
  //   S20 = out_2[20]; S21 = out_2[21]; S22 = out_2[22]; S23 = out_2[23]; S24 = out_2[24]; S25 = out_2[25];
  //   S26 = out_2[26]; S27 = out_2[27]; S28 = out_2[28]; S29 = out_2[29]; S30 = out_2[30]; S31 = out_2[31]
endmodule
